// Logisim project oisc.circ as structural Verilog: 1 circuit, main circuit main
module main (
  input  [7:0] DEBUG_IN,
  input  [15:0] T
);

  wire and_1_out, and_2_out, button_1_out, CLK, CLK1_out, comparator_1_eq, demultiplexer_2_out0,
       demultiplexer_2_out1, nor_2_out, nor_3_out, not_1_out, not_2_out, not_3_out, OE_ADDR, OE_ALU,
       OE_DBGIN, OE_DBGOUT, OE_IO, OE_MEM, OE_PC, OE_RAM, OE_ROM, SUFFIX_SELECT, WE_DBGOUT, WE_HADDR, WE_IO,
       WE_LADDR, WE_MEM, WE_PC, WE_RAM, WE_X, WE_Y, Z_DETECT;
  wire [2:0] ADDRESS, SUFFIX_BITS;
  wire [3:0] MICRO_ADDR;
  wire [7:0] buffer_1_out, controlled_buffer_6_out, DATA, HADDR_q, HPC_q, LADDR_q, LPC_q, NOR_out,
       register_1_q, X_q, Y_q;
  wire [15:0] ADDR_DIRECT, rom_2_data;

  Register #(.trigger("high")) X (.D(DATA), .en(1'b1), .Q(X_q), .clk(WE_X));  // open: clr
  Register #(.trigger("high")) Y (.D(DATA), .en(1'b1), .Q(Y_q), .clk(WE_Y));  // open: clr
  Register #(.trigger("high")) HPC (.D(ADDR_DIRECT[15:8]), .Q(HPC_q), .clk(WE_PC));  // open: en, clr
  assign ADDR_DIRECT[15:8] = OE_PC ? HPC_q : 8'bz;  // Controlled_Buffer controlled_buffer_1
  Register #(.trigger("high")) HADDR (.D(DATA), .Q(HADDR_q), .clk(WE_HADDR));  // open: en, clr
  assign ADDR_DIRECT[15:8] = OE_ADDR ? HADDR_q : 8'bz;  // Controlled_Buffer controlled_buffer_2
  assign NOR_out = ~(X_q | Y_q);  // NOR_Gate NOR, 8 bits wide
  assign DATA = OE_ALU ? NOR_out : 8'bz;  // Controlled_Buffer controlled_buffer_3
  assign ADDR_DIRECT[7:0] = OE_PC ? LPC_q : 8'bz;  // Controlled_Buffer controlled_buffer_4
  Register #(.trigger("high")) LPC (.D(ADDR_DIRECT[7:0]), .Q(LPC_q), .clk(WE_PC));  // open: en, clr
  Register #(.trigger("high")) LADDR (.D(DATA), .Q(LADDR_q), .clk(WE_LADDR));  // open: en, clr
  assign ADDR_DIRECT[7:0] = OE_ADDR ? LADDR_q : 8'bz;  // Controlled_Buffer controlled_buffer_5
  Multiplexer #(.width(3), .enable("false")) multiplexer_1 (
    .in0(ADDR_DIRECT[2:0]), .in1(SUFFIX_BITS), .out(ADDRESS), .sel(SUFFIX_SELECT));
  not not_1 (not_1_out, WE_RAM);
  assign controlled_buffer_6_out = WE_RAM ? buffer_1_out : 8'bz;  // Controlled_Buffer controlled_buffer_6
  assign buffer_1_out = DATA;  // Buffer buffer_1, 8 bits wide
  RAM #(.addrWidth(16), .bus("asynch")) ram_1 (
    .addr({ADDR_DIRECT[15:3], ADDRESS}), .data(controlled_buffer_6_out), .ld(not_1_out));  // open: sel, clr
  assign DATA = OE_RAM ? controlled_buffer_6_out : 8'bz;  // Controlled_Buffer controlled_buffer_7
  nor Z (Z_DETECT, NOR_out[0], NOR_out[1], NOR_out[2], NOR_out[3], NOR_out[4], NOR_out[5], NOR_out[6], NOR_out[7]);
  Clock CLK1 (.out(CLK1_out));
  or or_1 (CLK, CLK1_out, nor_2_out);
  Button button_1 (.out(button_1_out));
  nor nor_2 (nor_2_out, button_1_out, nor_3_out);
  nor nor_3 (nor_3_out, nor_2_out, and_2_out);
  // Probe on DATA
  // Probe on {ADDR_DIRECT[15:3], ADDRESS}
  Pull_Resistor pull_resistor_1 (.node({ADDR_DIRECT[15:3], ADDRESS}));
  Counter #(.width(4), .max('hf)) counter_1 (
    .Q(MICRO_ADDR), .clk(not_2_out), .clr(and_1_out));  // open: load, D, count, carry
  not not_2 (not_2_out, CLK);
  LED led_1 (.in(nor_3_out));
  ROM #(.addrWidth(15)) rom_1 (.addr({ADDR_DIRECT[14:3], ADDRESS}), .data(DATA), .sel(OE_ROM));
  and and_1 (and_1_out, MICRO_ADDR[1], MICRO_ADDR[3]);
  ROM #(.addrWidth(5), .dataWidth(16)) rom_2 (
    .addr({Z_DETECT, MICRO_ADDR}),
    .data({rom_2_data[15:12], SUFFIX_SELECT, SUFFIX_BITS, rom_2_data[7], WE_PC, WE_MEM, WE_HADDR, WE_LADDR, WE_X, WE_Y, rom_2_data[0]}),
    .sel(CLK));
  Demultiplexer #(.select(2), .enable("false")) demultiplexer_1 (
    .out2(WE_RAM), .out3(WE_IO), .in(WE_MEM), .sel(ADDR_DIRECT[15:14]));  // open: out0, out1
  Demultiplexer #(.select(2), .enable("false")) demultiplexer_2 (
    .out0(demultiplexer_2_out0), .out1(demultiplexer_2_out1), .out2(OE_RAM), .out3(OE_IO), .in(OE_MEM),
    .sel(ADDR_DIRECT[15:14]));
  Pull_Resistor pull_resistor_2 (.node({rom_2_data[15:12], SUFFIX_SELECT, SUFFIX_BITS, rom_2_data[7], WE_PC, WE_MEM, WE_HADDR, WE_LADDR, WE_X, WE_Y, rom_2_data[0]}));
  not not_3 (not_3_out, OE_MEM);
  and and_2 (and_2_out, not_3_out, comparator_1_eq);
  Comparator #(.width(16)) comparator_1 (
    .a({ADDR_DIRECT[15:3], ADDRESS}), .b(T), .eq(comparator_1_eq));  // open: gt, lt
  or or_2 (OE_ROM, demultiplexer_2_out0, demultiplexer_2_out1);
  buf buffer_2 (OE_ALU, rom_2_data[12]);
  buf buffer_3 (OE_MEM, rom_2_data[13]);
  buf buffer_4 (OE_PC, rom_2_data[14]);
  buf buffer_5 (OE_ADDR, rom_2_data[15]);
  LED led_2 (.in(DEBUG_IN[4]));
  LED led_3 (.in(DEBUG_IN[7]));
  LED led_4 (.in(DEBUG_IN[6]));
  LED led_5 (.in(DEBUG_IN[5]));
  Register #(.trigger("high")) register_1 (.D(DATA), .Q(register_1_q), .clk(WE_DBGOUT));  // open: en, clr
  LED led_6 (.in(register_1_q[6]));
  LED led_7 (.in(register_1_q[5]));
  LED led_8 (.in(register_1_q[7]));
  LED led_9 (.in(register_1_q[4]));
  Demultiplexer #(.enable("false")) demultiplexer_3 (.out0(OE_DBGOUT), .out1(OE_DBGIN), .in(OE_IO), .sel(ADDRESS[0]));
  Demultiplexer #(.enable("false")) demultiplexer_4 (.out0(WE_DBGOUT), .in(WE_IO), .sel(ADDRESS[0]));  // open: out1
  assign DATA = OE_DBGIN ? DEBUG_IN : 8'bz;  // Controlled_Buffer controlled_buffer_8
  LED led_10 (.in(DEBUG_IN[3]));
  LED led_11 (.in(DEBUG_IN[1]));
  LED led_12 (.in(DEBUG_IN[0]));
  LED led_13 (.in(DEBUG_IN[2]));
  assign DATA = OE_DBGOUT ? {8{1'b0}} : 8'bz;  // Controlled_Buffer controlled_buffer_9
  LED led_14 (.in(register_1_q[0]));
  LED led_15 (.in(register_1_q[1]));
  LED led_16 (.in(register_1_q[3]));
  LED led_17 (.in(register_1_q[2]));

  // Other names for the same wires on the sheet: ADDRESS[15:3] = ADDR_DIRECT[15:3]

  // Notes on the sheet:
  //   RAM
  //   ALU
  //   REGISTERS
  //   buffered for data holdoff (caps irl)
  //   PROGRAM ROM
  //   MAPPED MEMORY
  //   contents of rom_1 (hex, n*v repeats v):
  //   bf c2 7d 0 0 8 0 8 bf c2 7d 83 0 10 0 10 bf c3 7d 0 0 18 0 18 bf c3 7d 0 0 20 0 20 bf c4 7d 0 0 28 0
  //   28 bf c4 7d 41 0 30 0 30 bf c5 7d 0 0 38 0 38 bf c5 7d 38 0 40 0 40 bf c6 7d 0 0 48 0 48 bf c6 7d 41
  //   0 50 0 50 bf c7 7d 0 0 58 0 58 bf c7 7d 38 0 60 0 60 bf ca 7d 0 0 68 0 68 bf ca 7d 41 0 70 0 70 bf
  //   cb 7d 0 0 78 0 78 bf cb 7d 10 0 80 0 80 bf cc 7d 0 0 88 0 88 bf cc 7d 41 0 90 0 90 bf cd 7d 0 0 98 0
  //   98 bf cd 7d 20 0 a0 0 a0 bf ce 7d 0 0 a8 0 a8 bf ce 7d 41 0 b0 0 b0 bf cf 7d 0 0 b8 0 b8 bf cf 7d 20
  //   0 c0 0 c0 bf d0 7d 0 0 c8 0 c8 bf d0 7d 41 0 d0 0 d0 bf d1 7d 0 0 d8 0 d8 bf d1 7d 10 0 e0 0 e0 bf
  //   d2 7d 0 0 e8 0 e8 bf d2 7d 83 0 f0 0 f0 bf d3 7d 0 0 f8 0 f8 bf d3 7d 0 1 0 1 0 bf d4 7d 0 1 8 1 8
  //   bf d4 7d 41 1 10 1 10 bf d5 7d 0 1 18 1 18 bf d5 7d 28 1 20 1 20 bf d6 7d 0 1 28 1 28 bf d6 7d 41 1
  //   30 1 30 bf d7 7d 0 1 38 1 38 bf d7 7d 28 1 40 1 40 bf d8 7d 0 1 48 1 48 bf d8 7d 41 1 50 1 50 bf d9
  //   7d 0 1 58 1 58 bf d9 7d 10 1 60 1 60 bf dc 7d 0 1 68 1 68 bf dc 7d 41 1 70 1 70 bf dd 7d 0 1 78 1 78
  //   bf dd 7d 20 1 80 1 80 bf de 7d 0 1 88 1 88 bf de 7d 41 1 90 1 90 bf df 7d 0 1 98 1 98 bf df 7d 20 1
  //   a0 1 a0 bf e0 7d 0 1 a8 1 a8 bf e0 7d 41 1 b0 1 b0 bf e1 7d 0 1 b8 1 b8 bf e1 7d f 1 c0 1 c0 bf e2
  //   7d 0 1 c8 1 c8 bf e2 7d 83 1 d0 1 d0 bf e3 7d 0 1 d8 1 d8 bf e3 7d 0 1 e0 1 e0 80 7b 7d 0 1 e8 1 e8
  //   80 7b 7d e6 1 f0 1 f0 80 7c 7d 0 1 f8 1 f8 80 7c 7d 40 2 0 2 0 80 79 7d 0 2 8 2 8 80 79 80 7b 2 10 2
  //   10 80 79 80 79 2 18 2 18 80 7a 7d 0 2 20 2 20 80 7a 80 7c 2 28 2 28 80 7a 80 7a 2 30 2 30 80 7b 7d 0
  //   2 38 2 38 80 7b 7d 0 2 40 2 40 80 7b 80 7b 2 48 4 c0 80 7b 7d 0 2 50 2 50 80 7b 7d 0 2 58 2 58 80 7d
  //   7d 0 2 60 2 60 80 7d 7d 0 2 68 2 68 80 7d 80 7d 2 70 3 8 bf f0 7d 0 2 78 2 78 bf f0 c0 1 2 80 2 80
  //   bf f0 bf f0 2 88 2 88 80 7d 7d 0 2 90 2 90 80 7d bf f0 2 98 2 98 80 7d 80 7d 2 a0 2 a8 0 7d 0 7d 3 8
  //   3 8 80 7d 7d 0 2 b0 2 b0 80 7d 80 7b 2 b8 2 b8 80 7d 80 7d 2 c0 2 e0 80 7d 7d 0 2 c8 2 c8 80 7d 7d
  //   21 2 d0 2 d0 c0 0 80 7d 2 d8 2 d8 80 7b 80 7b 3 0 3 0 80 7d 7d 0 2 e8 2 e8 80 7d 7d 1 2 f0 2 f0 c0 0
  //   80 7d 2 f8 2 f8 80 7b 80 7b 3 0 3 0 80 7d 80 7d 2 58 2 58 80 20 7d 0 3 10 3 10 80 20 7d fd 3 18 3 18
  //   80 21 7d 0 3 20 3 20 80 21 7d d8 15 a0 15 a0 80 b 7d 0 3 30 3 30 80 b 7d fd 3 38 3 38 80 c 7d 0 3 40
  //   3 40 80 c 7d b8 c c8 c c8 80 27 7d 0 3 50 3 50 80 27 7d c3 3 58 3 58 80 25 7d 0 3 60 3 60 80 25 7d
  //   fd 3 68 3 68 80 26 7d 0 3 70 3 70 80 26 7d 88 18 58 18 58 80 27 7d 0 3 80 3 80 80 27 7d d7 3 88 3 88
  //   80 25 7d 0 3 90 3 90 80 25 7d fd 3 98 3 98 80 26 7d 0 3 a0 3 a0 80 26 7d 58 18 58 18 58 bf da 7d 0 3
  //   b0 3 b0 bf da 80 79 3 b8 3 b8 bf da bf da 3 c0 3 c0 bf db 7d 0 3 c8 3 c8 bf db 80 7a 3 d0 3 d0 bf db
  //   bf db 3 d8 3 d8 bf e6 7d 0 3 e0 3 e0 bf e6 7d fd 3 e8 3 e8 bf e7 7d 0 3 f0 3 f0 bf e7 7d 8 bf d0 bf
  //   d0 bf f0 bf f0 4 0 4 0 80 7c 7d 0 4 8 4 8 80 7c bf f0 4 10 4 10 80 7c 80 7c 4 18 4 18 80 27 7d 0 4
  //   20 4 20 80 27 80 7c 4 28 4 28 80 27 80 27 4 30 4 30 80 25 7d 0 4 38 4 38 80 25 7d fc 4 40 4 40 80 26
  //   7d 0 4 48 4 48 80 26 7d b0 18 58 18 58 80 27 7d 0 4 58 4 58 80 27 7d dd 4 60 4 60 80 25 7d 0 4 68 4
  //   68 80 25 7d fc 4 70 4 70 80 26 7d 0 4 78 4 78 80 26 7d 80 18 58 18 58 bf f0 7d 0 4 88 4 88 bf f0 c0
  //   1 4 90 4 90 bf f0 bf f0 4 98 4 98 80 7d 7d 0 4 a0 4 a0 80 7d bf f0 4 a8 4 a8 80 7d 80 7d 4 b0 4 b8
  //   80 7d 80 7d 4 80 4 80 80 7b 80 7b 2 30 2 30 80 79 80 79 4 c0 4 c0 80 81 7d 0 4 d0 4 d0 80 81 80 3 4
  //   d8 4 d8 80 81 80 4 4 e0 4 e0 80 82 7d 0 4 e8 4 e8 80 82 80 4 4 f0 4 f0 80 82 80 3 4 f8 4 f8 80 80 7d
  //   0 5 0 5 0 80 80 80 81 5 8 5 8 4*80 5 10 5 10 80 80 80 82 5 18 5 18 4*80 5 20 5 20 80 0 7d 0 5 28 5
  //   28 80 0 80 80 5 30 5 30 80 0 80 0 5 38 5 38 bf da 7d 0 5 40 5 40 bf da 7d 82 5 48 5 48 80 80 7d 0 5
  //   50 5 50 80 80 80 3 5 58 5 58 80 81 7d 0 5 60 5 60 80 81 80 4 5 68 5 68 80 80 80 81 5 70 5 70 bf db
  //   7d 0 5 78 5 78 bf db 80 80 5 80 5 80 bf db bf db 5 88 5 88 bf e6 7d 0 5 90 5 90 bf e6 7d fb 5 98 5
  //   98 bf e7 7d 0 5 a0 5 a0 bf e7 7d 58 bf d0 bf d0 bf f0 bf f0 5 b0 5 b0 80 7e 7d 0 5 b8 5 b8 80 7e bf
  //   f0 5 c0 5 c0 80 7e 80 7e 5 c8 5 c8 80 80 7d 0 5 d0 5 d0 80 80 80 7e 5 d8 5 d8 4*80 5 e0 7 0 80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
  //   MICROCODE
  //   contents of rom_2 (hex, n*v repeats v):
  //   6a10 6b08 a002 6810 6908 a004 9020 6c10 6d08 8040 1 5*0 6a10 6b08 a002 6810 6908 a004 9020 6e10 6f08
  //   8040 1
  //   I/O
endmodule
